// Logisim project 8_bit_cpu.circ as structural Verilog: 8 circuits, main circuit CPU
module CPU (
  output [9:0] out_1
);

  wire Branch, clk, control_unit_1_read, control_unit_1_we, control_unit_1_write, EQ, fulladder10_1_cout,
       fulladder10_2_cout, mux2;
  wire [1:0] and_1_out, bit_extender_1_out, mux1, PCmux;
  wire [2:0] alufunc, instruction_memory_1_rd, instruction_memory_1_rs, instruction_memory_1_rt;
  wire [3:0] opcode;
  wire [7:0] alu_out, IMM, mem_out, multiplexer_2_out, multiplexer_3_out, reg_file_1_rs_data,
       reg_file_1_rt_data;
  wire [9:0] Branch_Add, JMP, multiplexer_1_out, one_Add, PC_val;

  Clock clock_1 (.out(clk));
  assign bit_extender_1_out = {{1{Branch}}, Branch};  // Bit_Extender bit_extender_1
  assign and_1_out = PCmux & bit_extender_1_out;  // AND_Gate and_1, 2 bits wide
  Instruction_Memory instruction_memory_1 (
    .PC(PC_val), .IMM(IMM), .rd(instruction_memory_1_rd), .rt(instruction_memory_1_rt),
    .rs(instruction_memory_1_rs), .opcode(opcode), .JMP(JMP));
  Multiplexer #(.select(2), .width(10)) multiplexer_1 (
    .in0(one_Add), .in1(Branch_Add), .in2(JMP), .out(multiplexer_1_out), .sel(and_1_out));  // open: in3
  Register #(.trigger("falling"), .width(10)) PC_Register (
    .D(multiplexer_1_out), .en(1'b1), .clk(clk), .Q(PC_val));  // open: clr
  Control_Unit control_unit_1 (
    .opcode(opcode), .EQ(EQ), .mux1(mux1), .mux2(mux2), .WE(control_unit_1_we), .write(control_unit_1_write),
    .read(control_unit_1_read), .ALUfunc(alufunc), .PCmux(PCmux), .Branch(Branch));
  Multiplexer #(.select(2), .width(8)) multiplexer_2 (
    .in0(alu_out), .in1(mem_out), .in2(IMM), .in3({8{1'b0}}), .out(multiplexer_2_out), .sel(mux1));
  assign out_1 = {{2{IMM[7]}}, IMM};  // Bit_Extender bit_extender_2
  Reg_File reg_file_1 (
    .WE(control_unit_1_we), .rd(instruction_memory_1_rd), .data(multiplexer_2_out), .clk(clk),
    .rt(instruction_memory_1_rt), .rs(instruction_memory_1_rs), .rt_data(reg_file_1_rt_data),
    .rs_data(reg_file_1_rs_data));
  Multiplexer #(.width(8)) multiplexer_3 (.in0(reg_file_1_rt_data), .in1(IMM), .out(multiplexer_3_out), .sel(mux2));
  FULLADDER10 fulladder10_1 (.CIN(1'b0), .X(PC_val), .Y(out_1), .COUT(fulladder10_1_cout), .SUM(Branch_Add));
  FULLADDER10 fulladder10_2 (.CIN(1'b0), .X(PC_val), .Y(10'h1), .COUT(fulladder10_2_cout), .SUM(one_Add));
  Data_Memory data_memory_1 (
    .address(alu_out), .write(control_unit_1_write), .read(control_unit_1_read), .clk(clk),
    .write_data(reg_file_1_rt_data), .read_data(mem_out));
  ALU alu_1 (.X(reg_file_1_rs_data), .Y(multiplexer_3_out), .ALUfunc(alufunc), .Result(alu_out), .EQ(EQ));
  // also tied to GND on the sheet: {fulladder10_1_cout, fulladder10_2_cout}
endmodule

module Reg_File (
  input  WE,
  input  [2:0] rd,
  input  [7:0] data,
  input  clk,
  input  [2:0] rt,
  input  [2:0] rs,
  output [7:0] rt_data,
  output [7:0] rs_data
);

  wire decoder_1_out0, decoder_1_out1, decoder_1_out2, decoder_1_out3, decoder_1_out4, decoder_1_out5,
       decoder_1_out6, decoder_1_out7;
  wire [7:0] R0_q, R1_q, R2_q, R3_q, R4_q, R5_q, R6_q, R7_q;

  Decoder #(.select(3)) decoder_1 (
    .out0(decoder_1_out0), .out1(decoder_1_out1), .out2(decoder_1_out2), .out3(decoder_1_out3),
    .out4(decoder_1_out4), .out5(decoder_1_out5), .out6(decoder_1_out6), .out7(decoder_1_out7), .sel(rd),
    .en(WE));
  Multiplexer #(.select(3), .width(8)) multiplexer_1 (
    .in0(R0_q), .in1(R1_q), .in2(R2_q), .in3(R3_q), .in4(R4_q), .in5(R5_q), .in6(R6_q), .in7(R7_q),
    .out(rt_data), .sel(rt));
  Multiplexer #(.select(3), .width(8)) multiplexer_2 (
    .in0(R0_q), .in1(R1_q), .in2(R2_q), .in3(R3_q), .in4(R4_q), .in5(R5_q), .in6(R6_q), .in7(R7_q),
    .out(rs_data), .sel(rs));
  Register #(.trigger("falling")) R0 (.D(data), .en(decoder_1_out0), .clk(clk), .Q(R0_q));  // open: clr
  Register #(.trigger("falling")) R1 (.D(data), .en(decoder_1_out1), .clk(clk), .Q(R1_q));  // open: clr
  Register #(.trigger("falling")) R2 (.D(data), .en(decoder_1_out2), .clk(clk), .Q(R2_q));  // open: clr
  Register #(.trigger("falling")) R3 (.D(data), .en(decoder_1_out3), .clk(clk), .Q(R3_q));  // open: clr
  Register #(.trigger("falling")) R4 (.D(data), .en(decoder_1_out4), .clk(clk), .Q(R4_q));  // open: clr
  Register #(.trigger("falling")) R5 (.D(data), .en(decoder_1_out5), .clk(clk), .Q(R5_q));  // open: clr
  Register #(.trigger("falling")) R6 (.D(data), .en(decoder_1_out6), .clk(clk), .Q(R6_q));  // open: clr
  Register #(.trigger("falling")) R7 (.D(data), .en(decoder_1_out7), .clk(clk), .Q(R7_q));  // open: clr
endmodule

module Instruction_Memory (
  input  [9:0] PC,
  output [7:0] IMM,
  output [2:0] rd,
  output [2:0] rt,
  output [2:0] rs,
  output [3:0] opcode,
  output [9:0] JMP
);

  ROM #(.addrWidth(10), .dataWidth(21)) Instruction_Memory (.addr(PC), .data({opcode, rs, rt, rd[2], JMP[9:8], IMM}));

  assign JMP[7:0] = IMM;
  assign rd[1:0] = JMP[9:8];

  // Notes on the sheet:
  //   contents of Instruction_Memory (hex, n*v repeats v):
  //   60306 60601 6040c 1f700 1f3d00 b70fd 160008 b200
endmodule

module Data_Memory (
  input  [7:0] address,
  input  write,
  input  read,
  input  clk,
  input  [7:0] write_data,
  output [7:0] read_data
);

  RAM #(.asyncread("true"), .trigger("falling")) My_Ram (
    .addr(address), .we(write), .oe(read), .clk(clk), .din(write_data), .dout(read_data));
endmodule

module ALU (
  input  [7:0] X,
  input  [7:0] Y,
  input  [2:0] ALUfunc,
  output [7:0] Result,
  output EQ
);

  wire comparator_1_lt;
  wire [7:0] adder_1_out, and_1_out, bit_extender_1_out, multiplexer_1_out, or_1_out, shifter_1_out;

  Adder adder_1 (.a(X), .b(Y), .out(adder_1_out));  // open: cin, cout
  Shifter #(.shift("rl")) shifter_1 (.in(X), .\dist (Y[2:0]), .out(shifter_1_out));
  assign and_1_out = X & Y;  // AND_Gate and_1, 8 bits wide
  assign or_1_out = X | Y;  // OR_Gate or_1, 8 bits wide
  Multiplexer #(.select(2), .width(8)) multiplexer_1 (
    .in0(adder_1_out), .in1(and_1_out), .in2(or_1_out), .in3(shifter_1_out), .out(multiplexer_1_out),
    .sel(ALUfunc[1:0]));
  assign bit_extender_1_out = {{7{comparator_1_lt}}, comparator_1_lt};  // Bit_Extender bit_extender_1
  Comparator comparator_1 (.a(X), .b(Y), .eq(EQ), .lt(comparator_1_lt));  // open: gt
  Multiplexer #(.width(8)) multiplexer_2 (
    .in0(multiplexer_1_out), .in1(bit_extender_1_out), .out(Result), .sel(ALUfunc[2]));
endmodule

module Control_Unit (
  input  [3:0] opcode,
  input  EQ,
  output [1:0] mux1,
  output mux2,
  output WE,
  output write,
  output read,
  output [2:0] ALUfunc,
  output [1:0] PCmux,
  output Branch
);

  wire and_7_out, fulladder1_1_cout, not_1_out, not_2_out, not_3_out, not_4_out, not_5_out, not_6_out,
       PCmux0, xor_1_out;
  wire [1:0] and_5_out, multiplexer_2_out, not_7_out, not_8_out;

  not not_1 (not_1_out, opcode[2]);
  not not_2 (not_2_out, opcode[0]);
  not not_3 (not_3_out, opcode[2]);
  not not_4 (not_4_out, opcode[1]);
  xor xor_1 (xor_1_out, EQ, opcode[1]);
  and and_1 (mux1[1], opcode[1], not_1_out);
  or or_1 (mux2, write, mux1[0]);
  not not_5 (not_5_out, PCmux0);
  and and_2 (WE, not_5_out, not_6_out);
  not not_6 (not_6_out, write);
  and and_3 (write, not_2_out, opcode[1]);
  and and_4 (mux1[0], opcode[0], not_3_out, not_4_out);
  Multiplexer #(.select(2), .width(2)) multiplexer_1 (
    .in0(opcode[3:2]), .in1(opcode[3:2]), .in2(opcode[3:2]), .in3(not_7_out), .out(ALUfunc[1:0]),
    .sel(and_5_out));
  assign not_7_out = ~opcode[3:2];  // NOT_Gate not_7, 2 bits wide
  assign and_5_out = opcode[3:2] & opcode[1:0];  // AND_Gate and_5, 2 bits wide
  assign not_8_out = ~opcode[3:2];  // NOT_Gate not_8, 2 bits wide
  and and_6 (ALUfunc[2], and_5_out[0], and_5_out[1]);
  Multiplexer #(.select(2), .width(2)) multiplexer_2 (
    .in0(opcode[3:2]), .in1(opcode[3:2]), .in2(opcode[3:2]), .in3(not_8_out), .out(multiplexer_2_out),
    .sel(opcode[3:2]));
  and and_7 (and_7_out, PCmux[0], xor_1_out);
  assign PCmux = multiplexer_2_out & {2{opcode[0]}};  // AND_Gate and_8, 2 bits wide
  or or_2 (Branch, PCmux[1], and_7_out);
  FULLADDER1 fulladder1_1 (.X(PCmux[0]), .Y(PCmux[1]), .CIN(1'b0), .SUM(PCmux0), .COUT(fulladder1_1_cout));

  assign read = mux1[0];
  // also tied to GND on the sheet: fulladder1_1_cout

  // Other names for the same wires on the sheet: op1 = opcode[1]; op0 = opcode[0]; op2 = opcode[2]; op3 = opcode[3];
  //   read0 = mux1[0]; WE0 = WE; write0 = write
endmodule

module FULLADDER1 (
  input  X,
  input  Y,
  input  CIN,
  output SUM,
  output COUT
);

  wire and_1_out, and_2_out, xor_1_out;

  xor xor_1 (xor_1_out, X, Y);
  xor xor_2 (SUM, xor_1_out, CIN);
  and and_1 (and_1_out, xor_1_out, CIN);
  and and_2 (and_2_out, X, Y);
  or or_1 (COUT, and_1_out, and_2_out);
endmodule

module FULLADDER10 (
  input  CIN,
  input  [9:0] X,
  input  [9:0] Y,
  output COUT,
  output [9:0] SUM
);

  wire C0, C1, C2, C3, C4, C5, C6, C7, C8;

  FULLADDER1 fulladder1_1 (.X(X[0]), .Y(Y[0]), .CIN(CIN), .SUM(SUM[0]), .COUT(C0));
  FULLADDER1 fulladder1_2 (.X(X[1]), .Y(Y[1]), .CIN(C0), .SUM(SUM[1]), .COUT(C1));
  FULLADDER1 fulladder1_3 (.X(X[2]), .Y(Y[2]), .CIN(C1), .SUM(SUM[2]), .COUT(C2));
  FULLADDER1 fulladder1_4 (.X(X[3]), .Y(Y[3]), .CIN(C2), .SUM(SUM[3]), .COUT(C3));
  FULLADDER1 fulladder1_5 (.X(X[4]), .Y(Y[4]), .CIN(C3), .SUM(SUM[4]), .COUT(C4));
  FULLADDER1 fulladder1_6 (.X(X[5]), .Y(Y[5]), .CIN(C4), .SUM(SUM[5]), .COUT(C5));
  FULLADDER1 fulladder1_7 (.X(X[6]), .Y(Y[6]), .CIN(C5), .SUM(SUM[6]), .COUT(C6));
  FULLADDER1 fulladder1_8 (.X(X[7]), .Y(Y[7]), .CIN(C6), .SUM(SUM[7]), .COUT(C7));
  FULLADDER1 fulladder1_9 (.X(X[8]), .Y(Y[8]), .CIN(C7), .SUM(SUM[8]), .COUT(C8));
  FULLADDER1 fulladder1_10 (.X(X[9]), .Y(Y[9]), .CIN(C8), .SUM(SUM[9]), .COUT(COUT));

  // Other names for the same wires on the sheet: S0 = SUM[0]; S1 = SUM[1]; S2 = SUM[2]; S3 = SUM[3]; S4 = SUM[4];
  //   S5 = SUM[5]; S6 = SUM[6]; S7 = SUM[7]; S8 = SUM[8]; S9 = SUM[9]
endmodule
